# Fritzing sketch schematic (saved by Fritzing 0.9.3b)
breadboards: 1

parts:
  Part1 = Arduino Uno (Rev3)
  LCD1 = LCD screen
  Part2 = BME280 Breakout
  R1 = Resistor [tolerance=±5% resistance=2.2k package=THT]
  R2 = Resistor [tolerance=±5% resistance=2.2k package=THT]

nets:
  N1: Part1.D8, LCD1.DB3
  N2: Part1.D9_PWM, LCD1.DB4
  N3: Part1.D10_PWM/SS, LCD1.DB5
  N4: Part1.D11_PWM/MOSI, LCD1.DB6
  N5: Part1.D12/MISO, LCD1.DB7
  N6: Part1.A4/SDA, Part2.SDI/SDA, R2.Pin_0
  N7: Part1.A5/SCL, Part2.SCK/SCL, R1.Pin_0
  N8: Part1.D2, LCD1.RS
  N9: Part1.D3_PWM, LCD1.R/W
  N10: Part1.D4, LCD1.E
  N11: Part1.D5_PWM, LCD1.DB0
  N12: Part1.D6_PWM, LCD1.DB1
  N13: Part1.D7, LCD1.DB2
  3V3: Part1.3V3, Part2.3.3V
  5V: Part1.5V, LCD1.VDD
  GND: Part1.GND, LCD1.VSS, LCD1.V0, Part2.GND, R1.Pin_1, R2.Pin_1
